# Fritzing sketch sketch (saved by Fritzing 0.9.3b)
breadboards: 1

parts:
  U1 = ESP8266 WiFi Module [part_number=ESP8266]
  DHT1 = DHT11 Humitidy and Temperature Sensor
  R1 = Resistor [tolerance=±5% resistance=10k package="0805 [SMD]"]

nets:
  VCC: U1.VCC, DHT1.VDD, R1.Pin_1
  GND: U1.GND, DHT1.GND
  N1: U1.GPIO_13, DHT1.DATA, R1.Pin_0

custom parts:
  DHT11 Humitidy and Temperature Sensor: DHT11 Humidity and Temperature Sensor
