# Fritzing sketch sketch2 (saved by Fritzing 0.9.3b)
breadboards: 1

parts:
  U1 = LuaNode32 / ESP32 [part_number=ESP32S-PIN30]
  DHT1 = DHT11 Humitidy and Temperature Sensor
  R1 = Resistor [tolerance=±5% resistance=330 package="2010 [SMD]"]
  SW-1 = Vibration sensor module
  Part1 = MQ-4

nets:
  N1: U1.D35, Part1.AO
  GND: U1.GND, DHT1.GND, SW-1.Ground, Part1.GND
  VIN: U1.Vin, Part1.VCC
  3V3: U1.3V3, DHT1.VDD, R1.Pin_1, SW-1.vcc
  N2: U1.D2, U1.D4, DHT1.DATA, R1.Pin_0
  N3: U1.D18, SW-1.Digital_output

custom parts:
  LuaNode32 / ESP32: New Image for LuaNode32 DOIT ESP32 DEVKIT V1. Base parts from LuaNode32 / ESP32 ESP32 based LuaNode32 by G.Noorlander DOIT Esp32 DevKit v1 (30 pins long, 11 pins width) by Werner Rothschopf (modified by vanepp Dec 2018)
  DHT11 Humitidy and Temperature Sensor: DHT11 Humidity and Temperature Sensor
  Vibration sensor module: Single-roller type full induction trigger switch. When no vibration or tilt, the product is ON conduction state, and in the steady state, when a vibration or tilt, the switch will be rendered instantly disconnect the conductive resistance increases, generating a current pulse signal, thereby triggering circuit. The default state of the swith is close Digital output Supply voltage:3.3V-5V On-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
